# Fritzing sketch Frietzing schematic (saved by Fritzing 0.9.3b)
breadboards: 1

parts:
  Part1 = Arduino Nano (Rev3.0)
  S2 = Pushbutton [package="[THT]"]
  S4 = Pushbutton [package="[THT]"]
  S3 = Pushbutton [package="[THT]"]
  Part2 = Thumb Joystick
  S1 = Pushbutton [package="[THT]"]

nets:
  GND: Part1.GND, S2.Pin_1, S2.Pin_2, S4.Pin_1, S4.Pin_2, S3.Pin_1, S3.Pin_2, Part2.GND, S1.Pin_1, S1.Pin_2
  N1: Part1.D2, S1.Pin_3, S1.Pin_4
  N2: Part1.D3, S2.Pin_3, S2.Pin_4
  N3: Part1.D4, S3.Pin_3, S3.Pin_4
  N4: Part1.D5, S4.Pin_3, S4.Pin_4
  N5: Part1.D6, Part2.SEL
  5V: Part1.5V, Part2.VCC
  N6: Part1.A1, Part2.HORZ
  N7: Part1.A0, Part2.VERT
